# Fritzing sketch cat deterrent (saved by Fritzing 0.9.2b)
breadboards: 1

parts:
  Part1 = Arduino Uno (Rev3)
  Q1 = NPN-Transistor [package="TO92 [THT]"]
  D1 = Rectifier Diode [part_number=1N4001 package="300 mil [THT]"]
  R1 = Resistor [tolerance=±5% resistance=10k package=THT]
  R2 = Resistor [tolerance=±5% resistance=220 package=THT]
  M1 = DC Motor
  PIR1 = PIR sensor
  LED1 = LED - 5mm [color="Red (633nm)" package="5 mm [THT]"]

nets:
  N1: Part1.D11_PWM/MOSI, R2.Pin_0
  N2: Part1.D2, R1.Pin_1, PIR1.GND
  N3: Part1.D3_PWM, Q1.B
  5V: Part1.5V, D1.cathode, R1.Pin_0, M1.pin_2, PIR1.VDD
  N4: Part1.GND, Q1.E, PIR1.SIG, LED1.cathode
  N5: Q1.C, D1.anode, M1.pin_1
  N6: R2.Pin_1, LED1.anode
